# Fritzing sketch ArtNet Node (saved by Fritzing 0.9.1b)
circuit board: 8.35857cm x 5.46029cm
breadboards: 1

parts:
  Part1 = Arduino Mega 2560 (Rev3)
  J1 = female pin header, 4 pins [form="♀ (female)"]
  J2 = female pin header, 4 pins [form="♀ (female)"]
  J3 = female pin header, 3 pins [form="♀ (female)"]
  J4 = female pin header, 4 pins [form="♀ (female)"]
  J5 = female pin header, 4 pins [form="♀ (female)"]
  J6 = female pin header, 3 pins [form="♀ (female)"]
  J7 = female pin header, 4 pins [form="♀ (female)"]
  R1 = Resistor [tolerance=±5% resistance=150 package=THT]
  J8 = female pin header, 4 pins [form="♀ (female)"]
  R2 = Resistor [tolerance=±5% resistance=150 package=THT]
  R3 = Resistor [tolerance=±5% resistance=150 package=THT]
  J9 = female pin header, 4 pins [form="♀ (female)"]
  R4 = Resistor [tolerance=±5% resistance=10k package=THT]
  R5 = Resistor [tolerance=±5% resistance=10k package=THT]

nets:
  N1: Part1.A8, J9.pin1, R5.Pin_0
  N2: Part1.A9, J9.pin3, R4.Pin_0
  N3: Part1.D21/SCL, Part1.SCL, J7.pin1
  N4: Part1.D20/SDA, Part1.SDA, J7.pin2
  N5: Part1.D19/RX1, J5.pin4
  N6: Part1.D18/TX1, J5.pin1
  N7: Part1.GND, J2.pin1, J3.pin1, J4.pin1, J6.pin1, J7.pin4, J8.pin1, R4.Pin_1, R5.Pin_1
  N8: Part1.D11_PWM, R3.Pin_1
  N9: Part1.D10_PWM, R2.Pin_1
  N10: Part1.D9_PWM, R1.Pin_1
  N11: Part1.5V, J2.pin4, J4.pin4, J7.pin3, J9.pin2, J9.pin4
  N12: Part1.D0_RX0, J1.pin4
  N13: Part1.D1_TX0, J1.pin1
  N14: Part1.D2_PWM, J1.pin2, J1.pin3
  N15: Part1.D3_PWM, J5.pin2, J5.pin3
  N16: J2.pin2, J3.pin2
  N17: J2.pin3, J3.pin3
  N18: J4.pin2, J6.pin2
  N19: J4.pin3, J6.pin3
  N20: R1.Pin_0, J8.pin2
  N21: J8.pin3, R2.Pin_0
  N22: J8.pin4, R3.Pin_0
